# Fritzing sketch Battleship Diagram (saved by Fritzing 0.9.3b)

parts:
  Part1 = Arduino Uno (Rev3)
  Part2 = Arduino Uno (Rev3)
  Disp1 = LBT2088AH [part_number=LBT2088AH]
  Disp2 = LBT2088AH [part_number=LBT2088AH]
  KEYPAD1 = Membrane Matrix Keypad
  KEYPAD2 = Membrane Matrix Keypad

nets:
  N1: Part1.A4/SDA, Part2.A4/SDA
  N2: Part1.A5/SCL, Part2.A5/SCL
  N3: Part1.D8, KEYPAD1.1
  N4: Part1.D11_PWM/MOSI, Disp2.pin_5
  N5: Part1.D12/MISO, Disp2.pin_6
  N6: Part1.D13/SCK, Disp2.pin_7
  N7: Part1.D2, KEYPAD1.7
  N8: Part1.D3_PWM, KEYPAD1.6
  N9: Part1.D4, KEYPAD1.5
  N10: Part1.D5_PWM, KEYPAD1.4
  N11: Part1.D6_PWM, KEYPAD1.3
  N12: Part1.D7, KEYPAD1.2
  N13: Part1.5V, Disp2.pin1
  GND: Part1.GND, Part2.GND, Disp1.pin_8, Disp2.pin_8
  N14: Part2.D8, KEYPAD2.1
  N15: Part2.D11_PWM/MOSI, Disp1.pin_7
  N16: Part2.D12/MISO, Disp1.pin_6
  N17: Part2.D13/SCK, Disp1.pin_5
  N18: Part2.D2, KEYPAD2.7
  N19: Part2.D3_PWM, KEYPAD2.6
  N20: Part2.D4, KEYPAD2.5
  N21: Part2.D5_PWM, KEYPAD2.4
  N22: Part2.D6_PWM, KEYPAD2.3
  N23: Part2.D7, KEYPAD2.2
  N24: Part2.5V, Disp1.pin1

custom parts:
  Membrane Matrix Keypad: Membrane Matrix 3x4 Keypad
